// Logisim project riscv.circ as structural Verilog: 1 circuit, main circuit main
module main (
  input  in_1
);

  wire CLK, RESET;
  wire [7:0] counter_1_q, IRAM_data;

  Clock clock_1 (.out(CLK));
  Counter counter_1 (.clr(RESET), .clk(CLK), .Q(counter_1_q));  // open: load, up, count, D, carry
  _7_Segment_Display u_7_segment_display_1 ();  // open: g, f, a, b, e, d, c, dp
  // BCD_to_7_Segment_decoder bcd_to_7_segment_decoder_1: pin names not known
  // Binairy_to_BCD_converter #(.binvalue(8)) binairy_to_bcd_converter_1: pin names not known; wires that end beside it: counter_1_q
  _7_Segment_Display u_7_segment_display_2 ();  // open: g, f, a, b, e, d, c, dp
  // BCD_to_7_Segment_decoder bcd_to_7_segment_decoder_2: pin names not known
  POR por_1 (.out(RESET));
  ROM IRAM (.addr(counter_1_q), .data(IRAM_data));
  Register register_1 (.D(IRAM_data), .en(in_1), .clk(CLK));  // open: Q, clr
endmodule
